// Logisim project Lab2.circ as structural Verilog: 1 circuit, main circuit main
module main (
  input  X,
  output Y
);

  wire and_1_out, and_2_out, and_3_out, and_4_out, clock_1_out, D0_q, D0_qn, D1_q, D1_qn, D2_q, not_1_out,
       or_1_out, or_2_out, xor_1_out;

  not not_1 (not_1_out, X);
  and and_1 (and_1_out, D1_q, D0_qn);
  and and_2 (and_2_out, D1_q, D0_q, not_1_out);
  and and_3 (and_3_out, D2_q, D0_qn, X);
  xor xor_1 (xor_1_out, D1_q, D0_q);
  Clock clock_1 (.out(clock_1_out));
  and and_4 (and_4_out, not_1_out, xor_1_out);
  or or_1 (or_1_out, X, and_1_out);
  or or_2 (or_2_out, and_2_out, and_3_out);
  D_Flip_Flop D2 (.D(or_2_out), .clk(clock_1_out), .Q(D2_q));  // open: Qn, preset, reset
  D_Flip_Flop D1 (.D(and_4_out), .clk(clock_1_out), .Q(D1_q), .Qn(D1_qn));  // open: preset, reset
  D_Flip_Flop D0 (.D(or_1_out), .clk(clock_1_out), .Q(D0_q), .Qn(D0_qn));  // open: preset, reset
  and and_5 (Y, D2_q, D1_qn, D0_q);
endmodule
