// Logisim project Lab3.circ as structural Verilog: 1 circuit, main circuit main
module main (
  input  X1,
  input  X0,
  output out_3,
  output out_4,
  output out_5
);

  wire and_1_out, and_2_out, and_3_out, and_4_out, and_5_out, and_6_out, and_7_out, and_8_out, and_9_out,
       and_10_out, and_11_out, and_12_out, and_13_out, clock_1_out, not_1_out, not_2_out, not_3_out,
       not_4_out, not_5_out, not_6_out, or_1_out, or_2_out, or_3_out, T0_qn, T1_qn, T2_qn;

  not not_1 (not_1_out, X0);
  not not_2 (not_2_out, X0);
  and and_1 (and_1_out, out_5, T2_qn);
  not not_3 (not_3_out, X0);
  not not_4 (not_4_out, X1);
  and and_2 (and_2_out, T0_qn, T1_qn, X1, not_1_out);
  and and_3 (and_3_out, X1, T2_qn, T0_qn, out_4);
  and and_4 (and_4_out, out_3, out_4, X0, X1);
  and and_5 (and_5_out, X0, X1, T2_qn, out_5);
  and and_6 (and_6_out, not_3_out, not_4_out, out_5);
  and and_7 (and_7_out, X0, X1);
  or or_1 (or_1_out, and_1_out, T0_qn);
  and and_8 (and_8_out, and_7_out, or_1_out);
  or or_2 (or_2_out, and_2_out, and_3_out, and_4_out, and_5_out, and_6_out);
  or or_3 (or_3_out, not_2_out, and_8_out);
  Clock clock_1 (.out(clock_1_out));
  not not_5 (not_5_out, X1);
  not not_6 (not_6_out, X0);
  and and_9 (and_9_out, not_5_out, not_6_out, out_5, out_4);
  and and_10 (and_10_out, X0, X1, out_3);
  and and_11 (and_11_out, X1, out_3, out_4, T2_qn);
  and and_12 (and_12_out, out_5, out_4, T2_qn, X1, X0);
  and and_13 (and_13_out, X0, X1, T2_qn, T1_qn);
  or or_4 (out_3, and_9_out, and_10_out, and_11_out, and_12_out, and_13_out);
  T_Flip_Flop T2 (.T(out_3), .clk(clock_1_out), .Q(out_3), .Qn(T2_qn));  // open: reset, preset
  T_Flip_Flop T1 (.T(or_2_out), .clk(clock_1_out), .Q(out_4), .Qn(T1_qn));  // open: reset, preset
  T_Flip_Flop T0 (.T(or_3_out), .clk(clock_1_out), .Q(out_5), .Qn(T0_qn));  // open: reset, preset
endmodule
