// Logisim project MK_POCY_LAB4.circ as structural Verilog: 3 circuits, main circuit main
module main (
  input  [7:0] A,
  input  [7:0] B,
  input  [2:0] S,
  output O,
  output [7:0] Y,
  output E
);

  wire adder_1_cout, and_3_out, nor_1_out, not_2_out, or_2_out;
  wire [0:0] or_1_out, xor_1_out;
  wire [7:0] adder_1_out, and_1_out, divider_1_out, multiplier_1_cout, multiplier_1_out, not_1_out, xor_2_out;

  Divider #(.mode("twosComplement")) divider_1 (
    .a({4'b0000, A[3:0]}), .b(B), .out(divider_1_out), .upper({A[7:4], 4'b0000}));  // open: rem
  Adder adder_1 (.a(A), .b(B), .out(adder_1_out), .cout(adder_1_cout));  // open: cin
  nor nor_1 (nor_1_out, B[0], B[1], B[2], B[3], B[4], B[5], B[6], B[7]);
  Multiplier #(.mode("twosComplement")) multiplier_1 (
    .a(A), .b(B), .out(multiplier_1_out), .cout(multiplier_1_cout));  // open: cin
  ExactlyOne xor_1 (
    .out(xor_1_out[0]), .in0(B[0]), .in1(B[1]), .in2(B[2]), .in3(B[3]), .in4(B[4]), .in5(B[5]), .in6(B[6]),
    .in7(B[7]));
  assign and_1_out = A & B;  // AND_Gate and_1, 8 bits wide
  or or_1 (or_1_out[0], A[0], A[1], A[2], A[3], A[4], A[5], A[6], A[7]);
  assign xor_2_out = A ^ B;  // XOR_Gate xor_2, 8 bits wide
  or or_2 (or_2_out, multiplier_1_cout[0], multiplier_1_cout[1], multiplier_1_cout[2], multiplier_1_cout[3], multiplier_1_cout[4], multiplier_1_cout[5], multiplier_1_cout[6], multiplier_1_cout[7]);
  or or_3 (O, or_2_out, adder_1_cout);
  assign not_1_out = ~A;  // NOT_Gate not_1, 8 bits wide
  and and_2 (E, nor_1_out, and_3_out);
  Multiplexer #(.select(3), .width(8)) multiplexer_1 (
    .in0(multiplier_1_out), .in1(not_1_out), .in2({{7{1'b0}}, xor_1_out[0]}), .in3(divider_1_out),
    .in4(and_1_out), .in5(adder_1_out), .in6({{7{1'b0}}, or_1_out[0]}), .in7(xor_2_out), .out(Y), .sel(S));
  not not_2 (not_2_out, S[2]);
  and and_3 (and_3_out, S[0], S[1], not_2_out);
endmodule

module W1 (
  input  [7:0] A,
  input  [2:0] in_2,
  input  [7:0] B,
  input  [2:0] in_4,
  input  [2:0] in_5,
  input  [2:0] in_6,
  output [7:0] Wyjscie
);

  wire [2:0] undriven, undriven_2;
  wire [7:0] main_1_y, main_2_y, main_3_y;

  main main_1 (.A(A), .S(in_2), .Y(main_1_y));  // open: B, O, E
  main main_2 (.A(main_1_y), .B(B), .S(undriven), .Y(main_2_y));  // open: O, E
  main main_3 (.A(main_2_y), .S(in_5), .Y(main_3_y));  // open: B, O, E
  main main_4 (.A(main_3_y), .B(A), .S(undriven_2), .Y(Wyjscie));  // open: O, E
endmodule

module W2 (
  input  [7:0] A,
  input  [7:0] B,
  input  [2:0] in_3,
  input  [2:0] in_4,
  input  [2:0] in_5,
  input  [7:0] in_6,
  input  [2:0] in_7,
  input  [2:0] in_8,
  input  [2:0] in_9,
  output [7:0] Wyjsice
);

  wire [7:0] main_1_y, main_2_y, main_3_y, main_4_y, main_5_y;

  main main_1 (.A(B), .S(in_5), .Y(main_1_y));  // open: B, O, E
  main main_2 (.A(A), .B(B), .S(in_7), .Y(main_2_y));  // open: O, E
  main main_3 (.A(main_1_y), .B(in_6), .S(in_3), .Y(main_3_y));  // open: O, E
  main main_4 (.A(main_2_y), .S(in_8), .Y(main_4_y));  // open: B, O, E
  main main_5 (.A(B), .B(main_3_y), .S(in_4), .Y(main_5_y));  // open: O, E
  main main_6 (.A(main_4_y), .B(main_5_y), .S(in_9), .Y(Wyjsice));  // open: O, E
endmodule
