// Logisim project Lab5.circ as structural Verilog: 1 circuit, main circuit main
module main (
  input  Reset,
  input  [3:0] x_in
);

  wire clk_out, comparator_1_eq, not_1_out;
  wire [2:0] counter_1_q;
  wire [5:0] adder_1_out, bit_extender_1_out, register_1_q;

  Clock clk (.out(clk_out));
  assign bit_extender_1_out = {{2{1'b0}}, x_in};  // Bit_Extender bit_extender_1
  Adder #(.width(6)) adder_1 (.a(bit_extender_1_out), .b(register_1_q), .out(adder_1_out));  // open: cin, cout
  Register #(.width(6)) register_1 (.D(adder_1_out), .en(not_1_out), .clk(clk_out), .Q(register_1_q), .clr(Reset));
  Counter #(.max('h7), .width(3)) counter_1 (
    .count(not_1_out), .Q(counter_1_q), .clk(clk_out), .clr(Reset));  // open: load, D, carry, up
  not not_1 (not_1_out, comparator_1_eq);
  Comparator #(.width(3)) comparator_1 (.a(counter_1_q), .b(3'b100), .eq(comparator_1_eq));  // open: gt, lt
  Hex_Digit_Display hex_digit_display_1 (.value(register_1_q[5:2]));  // open: dp
endmodule
